// Logisim project alarma_seguridad.circ as structural Verilog: 1 circuit, main circuit main
module main (
  input  A,
  input  B,
  input  C,
  input  D,
  output W,
  output X,
  output Y,
  output Z
);

  wire and_1_out, and_2_out, and_3_out, and_4_out, and_5_out, and_6_out, and_7_out, or_1_out, or_2_out,
       or_4_out, or_6_out, or_8_out;

  or or_1 (or_1_out, D, C);
  or or_2 (or_2_out, B, A);
  and and_1 (and_1_out, A, D);
  and and_2 (and_2_out, A, C);
  and and_3 (and_3_out, C, D);
  and and_4 (and_4_out, A, D);
  and and_5 (and_5_out, A, C);
  and and_6 (and_6_out, A, B);
  not not_1 (Z, A);
  or or_3 (W, or_1_out, or_2_out);
  or or_4 (or_4_out, and_1_out, and_2_out);
  or or_5 (X, or_4_out, and_7_out);
  and and_7 (and_7_out, A, B);
  or or_6 (or_6_out, and_3_out, and_4_out);
  or or_7 (Y, or_6_out, or_8_out);
  or or_8 (or_8_out, and_5_out, and_6_out);
endmodule
