// Logisim project cepilladora.circ as structural Verilog: 1 circuit, main circuit main
module main (
  input  BD,
  input  BI,
  input  BP,
  input  LSD,
  input  LSI,
  input  MD,
  input  MI
);

  // OR_Gate or_1 has open pins: in0=LSI, in1=BD, out=open
endmodule
