// Logisim project cepilladora_2.circ as structural Verilog: 1 circuit, main circuit main
module main (
  input  BP,
  input  LSD,
  input  LSI,
  input  BD,
  input  BI,
  output MD,
  output MI
);

  wire and_1_out, and_2_out, and_3_out, and_4_out, not_1_out, not_2_out, not_3_out, not_4_out, not_5_out,
       not_6_out, not_7_out, not_8_out, not_9_out, not_10_out, not_11_out, not_12_out;

  not not_1 (not_1_out, BP);
  not not_2 (not_2_out, LSD);
  not not_3 (not_3_out, BI);
  not not_4 (not_4_out, BP);
  not not_5 (not_5_out, LSD);
  not not_6 (not_6_out, BD);
  not not_7 (not_7_out, BP);
  not not_8 (not_8_out, LSI);
  not not_9 (not_9_out, BD);
  not not_10 (not_10_out, BP);
  not not_11 (not_11_out, LSI);
  not not_12 (not_12_out, BI);
  and and_1 (and_1_out, not_1_out, not_2_out, BD, not_3_out);
  and and_2 (and_2_out, not_4_out, not_5_out, LSI, not_6_out);
  and and_3 (and_3_out, not_7_out, not_8_out, not_9_out, BI);
  and and_4 (and_4_out, not_10_out, LSD, not_11_out, not_12_out);
  or or_1 (MD, and_1_out, and_2_out);
  or or_2 (MI, and_3_out, and_4_out);
endmodule
