// Logisim project electroneumatica.circ as structural Verilog: 2 circuits, main circuit main
module main (
  input  S1,
  input  S2,
  input  B1,
  input  B2,
  output Y1,
  output Y2,
  output FALLA
);

  wire and_1_out, and_2_out, and_3_out, and_4_out, and_5_out, not_1_out, not_2_out, not_3_out, not_4_out,
       not_5_out, not_6_out, or_1_out, or_2_out;

  and and_1 (and_1_out, S1, S2);
  and and_2 (and_2_out, B1, not_1_out);
  not not_1 (not_1_out, B2);
  not not_2 (not_2_out, S1);
  and and_3 (and_3_out, not_2_out, not_3_out);
  not not_3 (not_3_out, B2);
  not not_4 (not_4_out, B1);
  not not_5 (not_5_out, S1);
  and and_4 (and_4_out, not_5_out, S2);
  and and_5 (and_5_out, S1, not_6_out);
  not not_6 (not_6_out, S2);
  and and_6 (FALLA, B1, B2);
  and and_7 (Y1, and_1_out, and_2_out);
  or or_1 (or_1_out, and_3_out, not_4_out);
  or or_2 (or_2_out, and_4_out, and_5_out);
  or or_3 (Y2, or_1_out, or_2_out);
endmodule

module electroneumatica (
  input  S1,
  input  S2,
  input  B1,
  input  B2,
  output Y1,
  output Y2,
  output FALLA
);

  wire and_1_out, and_3_out, and_4_out, and_5_out, and_6_out, and_7_out, and_8_out, and_9_out, not_1_out,
       not_2_out, not_3_out, not_4_out, not_5_out, not_6_out, not_7_out, not_8_out, or_1_out, or_3_out;

  not not_1 (not_1_out, B2);
  not not_2 (not_2_out, S1);
  not not_3 (not_3_out, S2);
  not not_4 (not_4_out, S1);
  not not_5 (not_5_out, S2);
  and and_1 (and_1_out, S1, S2);
  and and_2 (Y1, and_1_out, and_3_out);
  and and_3 (and_3_out, B1, not_1_out);
  or or_1 (or_1_out, not_2_out, not_3_out);
  or or_2 (Y2, or_1_out, not_6_out);
  not not_6 (not_6_out, B1);
  and and_4 (and_4_out, not_4_out, not_5_out);
  and and_5 (and_5_out, and_4_out, B2);
  and and_6 (and_6_out, B1, B2);
  and and_7 (and_7_out, S1, S2);
  not not_7 (not_7_out, B1);
  and and_8 (and_8_out, not_7_out, not_8_out);
  not not_8 (not_8_out, B2);
  or or_3 (or_3_out, and_5_out, and_6_out);
  and and_9 (and_9_out, and_7_out, and_8_out);
  or or_4 (FALLA, or_3_out, and_9_out);
endmodule
