# Fritzing sketch verifica_compuertas (saved by Fritzing 0.9.3b)
breadboards: 1

parts:
  U1 = SN74LS32N [package="DIP14 [THT]"]
  PSU1 = Adjustable Breadboard Power Supply
  SW1 = DIP Switch 8 Position [package=dipswitch-08]
  R1 = Resistor [tolerance=±5% resistance=1k package=THT]
  R2 = Resistor [tolerance=±5% resistance=1k package=THT]
  R3 = Resistor [tolerance=±5% resistance=1k package=THT]
  R4 = Resistor [tolerance=±5% resistance=1k package=THT]
  LED1 = LED - 5mm [color="Red (635nm)" package="5 mm [THT]"]
  R5 = Resistor [tolerance=±5% resistance=330 package=THT]

nets:
  N1: U1.1A, SW1.1, R1.Pin_0
  N2: U1.1B, SW1.2, R2.Pin_0
  N3: U1.1Y, LED1.anode
  N4: U1.GND, PSU1.Vout-, R1.Pin_1, R2.Pin_1, R3.Pin_1, R4.Pin_1, R5.Pin_1
  N5: U1.Vcc, PSU1.Vout+, SW1.13, SW1.14, SW1.15, SW1.16
  N6: SW1.3, R3.Pin_0
  N7: SW1.4, R4.Pin_0
  N8: LED1.cathode, R5.Pin_0

notes:
  Fuente de 5V
