# Fritzing sketch verifica_compuertas_mult (saved by Fritzing 0.9.3b)
breadboards: 2

parts:
  U1 = SN74LS32N [package="DIP14 [THT]"]
  PSU1 = Adjustable Breadboard Power Supply
  SW1 = DIP Switch 8 Position [package=dipswitch-08]
  R1 = Resistor [tolerance=±5% resistance=1k package=THT]
  R2 = Resistor [tolerance=±5% resistance=1k package=THT]
  R3 = Resistor [tolerance=±5% resistance=1k package=THT]
  R4 = Resistor [tolerance=±5% resistance=1k package=THT]
  Voltmeter_(DC)1 = Multimeter (DC Voltage)
  U2 = SN74LS32N [package="DIP14 [THT]"]
  PSU2 = Adjustable Breadboard Power Supply
  SW2 = DIP Switch 8 Position [package=dipswitch-08]
  R5 = Resistor [tolerance=±5% resistance=1k package=THT]
  R6 = Resistor [tolerance=±5% resistance=1k package=THT]
  R7 = Resistor [tolerance=±5% resistance=1k package=THT]
  R8 = Resistor [tolerance=±5% resistance=1k package=THT]
  Voltmeter_(DC)2 = Multimeter (DC Voltage)

nets:
  N1: U1.1A, SW1.1, R1.Pin_0
  N2: U1.1B, SW1.2, R2.Pin_0
  N3: U1.1Y, Voltmeter_(DC)1.V_Probe
  N4: U1.GND, PSU1.Vout-, R1.Pin_1, R2.Pin_1, R3.Pin_1, R4.Pin_1, Voltmeter_(DC)1.COM_Probe
  N5: U1.Vcc, PSU1.Vout+, SW1.13, SW1.14, SW1.15, SW1.16
  N6: SW1.3, R3.Pin_0
  N7: SW1.4, R4.Pin_0
  N8: U2.1A, SW2.1, R8.Pin_0
  N9: U2.1B, SW2.2, R7.Pin_0, Voltmeter_(DC)2.V_Probe
  N10: U2.GND, PSU2.Vout-, R5.Pin_1, R6.Pin_1, R7.Pin_1, R8.Pin_1, Voltmeter_(DC)2.COM_Probe
  N11: U2.Vcc, PSU2.Vout+, SW2.13, SW2.14, SW2.15, SW2.16
  N12: SW2.3, R6.Pin_0
  N13: SW2.4, R5.Pin_0

notes:
  Fuente de 5V

custom parts:
  Multimeter (DC Voltage): A standard multimeter to measure volatages, currents and resistances
