// Logisim project alarma_ejercicio.circ as structural Verilog: 1 circuit, main circuit main
module main (
  input  ALARMA,
  input  SENSOR_HUMO,
  input  SENSOR_PUERTA,
  input  SENSOR_VENTANA_1,
  input  SENSOR_VENTANA_2,
  output BUZZER,
  output EXTRACTOR,
  output STATUS,
  output LED_INDICADOR
);

  or or_1 (LED_INDICADOR, SENSOR_VENTANA_2, SENSOR_VENTANA_1, SENSOR_PUERTA, SENSOR_HUMO);

  assign BUZZER = ALARMA;
  assign EXTRACTOR = SENSOR_HUMO;
  assign STATUS = ALARMA;
endmodule
