// Logisim project carrito_seguidor_luz.circ as structural Verilog: 1 circuit, main circuit main
module main (
  input  S1,
  input  S2,
  input  S3,
  output M1,
  output M2,
  output ERROR
);

  wire and_1_out, and_2_out, and_3_out, and_4_out, not_1_out, not_2_out, not_3_out, not_4_out, not_5_out,
       not_6_out;

  not not_1 (not_1_out, S1);
  not not_2 (not_2_out, S3);
  not not_3 (not_3_out, S1);
  not not_4 (not_4_out, S2);
  not not_5 (not_5_out, S3);
  not not_6 (not_6_out, S2);
  and and_1 (and_1_out, not_1_out, S2);
  and and_2 (and_2_out, S2, not_2_out);
  and and_3 (and_3_out, not_3_out, not_4_out, not_5_out);
  and and_4 (and_4_out, S1, not_6_out, S3);
  or or_1 (M1, S3, and_1_out);
  or or_2 (M2, and_2_out, S1);
  or or_3 (ERROR, and_3_out, and_4_out);
endmodule
