// Logisim project contro_luces_inteligentes.circ as structural Verilog: 1 circuit, main circuit main
module main (
  input  S1,
  input  S2,
  input  S3,
  output L1,
  output L2,
  output L3
);

  wire and_2_out, and_3_out, not_1_out, not_2_out, not_3_out, not_4_out, not_5_out;

  not not_1 (not_1_out, S3);
  not not_2 (not_2_out, S3);
  not not_3 (not_3_out, S1);
  not not_4 (not_4_out, S2);
  not not_5 (not_5_out, S3);
  or or_1 (L1, not_1_out, S1);
  and and_1 (L2, S1, not_2_out);
  and and_2 (and_2_out, not_3_out, S2);
  and and_3 (and_3_out, S1, not_4_out, not_5_out);
  or or_2 (L3, and_2_out, and_3_out);
endmodule
