// Logisim project estacionamiento.circ as structural Verilog: 1 circuit, main circuit main
module main (
  input  AUTO,
  input  S1,
  input  S2,
  input  S3,
  output PLUMA
);

  wire and_1_out, and_2_out, and_3_out, not_1_out, not_2_out, not_3_out;

  not not_1 (not_1_out, S1);
  not not_2 (not_2_out, S2);
  not not_3 (not_3_out, S3);
  and and_1 (and_1_out, AUTO, not_1_out);
  and and_2 (and_2_out, AUTO, not_2_out);
  and and_3 (and_3_out, AUTO, not_3_out);
  or or_1 (PLUMA, and_1_out, and_2_out, and_3_out);
endmodule
